# Fritzing sketch CTPowerMonitor (saved by Fritzing 0.9.10b)
circuit board: 3.66298cm x 2.87311cm
breadboards: 1

parts:
  C1 = Tantalum Capacitor [capacitance=10µF voltage=35V package="100 mil [THT, tantalum]"]
  Burden = Resistor [tolerance=±5% power=0.25 resistance=33 package=THT]
  R1 = Resistor [tolerance=±5% power=0.25 resistance=10k package=THT]
  R2 = Resistor [tolerance=±5% power=0.25 resistance=10k package=THT]
  J1 = male alternating pin header, 3 pins [form="♂ (male)"]
  TRS1 = Audio Jack (TRS) 3.5mm [package="4Ucon 08780 [THT]"]

nets:
  GND: C1.-, R2.Pin_1, J1.pin3
  N1: C1.+, Burden.Pin_1, R1.Pin_1, R2.Pin_0, TRS1.Tip
  N2: Burden.Pin_0, J1.pin2, TRS1.Sleeve
  N3: R1.Pin_0, J1.pin1
